# Fritzing sketch fan (saved by Fritzing 0.9.6b)
circuit board: 11.4441cm x 6.95677cm
breadboards: 1

parts:
  C3 = Ceramic Capacitor [capacitance=0.1µF package="1206 [SMD, multilayer]"]
  C4 = Capacitor Polarized [part_number=1000μF package=panasonic_h13]
  U17 = ESP8266 WiFi Module [part_number=ESP8266]
  HI = Resistor [tolerance=±5% resistance=10k power=0.25 package=THT]
  MED = Resistor [tolerance=±5% resistance=10k power=0.25 package=THT]
  3 = Header 1 [package=1x01_offset]
  LOW = Resistor [tolerance=±5% resistance=10k power=0.25 package=THT]
  4 = Header 1 [package=1x01_offset]
  OFF = Resistor [tolerance=±5% resistance=10k power=0.25 package=THT]
  5 = Header 1 [package=1x01_offset]
  REV = Resistor [tolerance=±5% resistance=10k power=0.25 package=THT]
  6 = Header 1 [package=1x01_offset]
  UP = Resistor [tolerance=±5% resistance=10k power=0.25 package=THT]
  7 = Header 1 [package=1x01_offset]
  DOWN = Resistor [tolerance=±5% resistance=10k power=0.25 package=THT]
  2 = Header 1 [package=1x01_offset]
  1 = Header 1 [package=1x01_offset]
  GND = Header 1 [package=1x01_offset]
  VCC = Header 1 [package=1x01_offset]
  R1 = Resistor [tolerance=±5% resistance=10k power=0.25 package=THT]
  DS2 = DS18B20 1-Wire Temperature Sensor [part_number=DS18B20]
  R9 = Resistor [tolerance=±5% resistance=4.7k power=0.25 package=THT]
  Q1 = npn-Powertransistor [package="TO220 [THT]"]
  Q2 = npn-Powertransistor [package="TO220 [THT]"]
  Q3 = npn-Powertransistor [package="TO220 [THT]"]
  Q4 = npn-Powertransistor [package="TO220 [THT]"]
  Q5 = npn-Powertransistor [package="TO220 [THT]"]
  Q6 = npn-Powertransistor [package="TO220 [THT]"]
  Q7 = npn-Powertransistor [package="TO220 [THT]"]
  Q8 = npn-Powertransistor [package="TO220 [THT]"]
  DIP = Resistor [tolerance=±5% resistance=10k power=0.25 package=THT]
  8 = Header 1 [package=1x01_offset]
  AMS1117_3_3V = Voltage Regulator [package=to220-adj]
  Part1 = Adafruit Micro USB Breakout [part_number="Adafruit #1833"]
  5V_to_12V = Mini-360 DC-DC Buck converter [package=THT]

nets:
  GND: C3.0, C4.-, U17.GND, GND.1, DS2.GND, Q1.emitter, Q2.emitter, Q3.emitter, Q4.emitter, Q5.emitter, Q6.emitter, Q7.emitter, Q8.emitter, AMS1117_3_3V.ADJ, Part1.GND, 5V_to_12V.IN-, 5V_to_12V.OUT-
  3.3V: C3.1, C4.+, U17.VCC, U17.CH_PD, U17.REST, R1.Pin_0, DS2.VDD, R9.Pin_0, AMS1117_3_3V.OUT
  N1: U17.GPIO_0, R1.Pin_1, DIP.Pin_0
  N2: U17.GPIO_2, DS2.DQ, R9.Pin_1
  N3: U17.GPIO_15, LOW.Pin_0
  N4: U17.GPIO_4, HI.Pin_0
  N5: U17.GPIO_5, MED.Pin_0
  N6: U17.GPIO_16, DOWN.Pin_0
  N7: U17.GPIO_14, UP.Pin_0
  N8: U17.GPIO_12, REV.Pin_0
  N9: U17.GPIO_13, OFF.Pin_0
  N10: HI.Pin_1, Q1.base
  N11: MED.Pin_1, Q2.base
  N12: 3.1, Q3.collector
  N13: LOW.Pin_1, Q3.base
  N14: 4.1, Q4.collector
  N15: OFF.Pin_1, Q4.base
  N16: 5.1, Q5.collector
  N17: REV.Pin_1, Q5.base
  N18: 6.1, Q6.collector
  N19: UP.Pin_1, Q6.base
  N20: 7.1, Q7.collector
  N21: DOWN.Pin_1, Q7.base
  N22: 2.1, Q2.collector
  N23: 1.1, Q1.collector
  N24: VCC.1, 5V_to_12V.OUT+
  N25: Q8.base, DIP.Pin_1
  N26: Q8.collector, 8.1
  N27: AMS1117_3_3V.IN, Part1.VBUS, 5V_to_12V.IN+

custom parts:
  ESP8266 WiFi Module: Generic WiFi Module based on the ESP8266 with onboard PCB antenna and UART communications
  Adafruit Micro USB Breakout: Simple but effective - this breakout board has a USB Micro-B connector, with all 5 pins broken out. Great for pairing with a microcontroller with USB support, or adding USB 5V power to a project. We use a micro-AB connector with through-hole shielding pads for an excellent strong connection - it won't rip off by accident! Comes with one fully assembled and tested micro B breakout PCB and a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
  Mini-360 DC-DC Buck converter: Mini-360 DC-DC Buck converter. Tiny buck step down voltage converter, input voltage 4.75 to 23V output 1 to 17V adjustable. Available from ebay and the like.
